# Fritzing sketch scheme (saved by Fritzing 0.9.9b)
breadboards: 1

parts:
  part = RFID-RC522-v2
  part_2 = OLED 128x64 I2C Monochrome Display
  part_3 = KY-040 Rotary encoder [package="Breakout board"]
  Компонент2 = Arduino Mini (Rev5)
  S1 = Pushbutton [package="[THT]"]
  S2 = Pushbutton [package="[THT]"]
  R3 = Resistor [tolerance=±5% resistance=220 package=THT]
  R2 = Resistor [tolerance=±5% resistance=220 package=THT]
  R1 = Resistor [tolerance=±5% resistance=220 package=THT]
  S3 = Pushbutton [package="[THT]"]

nets:
  N1: part.SDA, Компонент2.D10_PWM
  N2: part.SCK, Компонент2.D13
  N3: part.MOSI, Компонент2.D11_PWM
  N4: part.MISO, Компонент2.D12
  GND: part.GND, part_2.GND, part_3.GND, Компонент2.GND, R3.Pin_0, R2.Pin_0, R1.Pin_0
  3.3V: part.3.3V, part_2.VDD, part_3.Vcc, Компонент2.5V, S1.Pin_1, S1.Pin_2, S2.Pin_1, S2.Pin_2, S3.Pin_1, S3.Pin_2
  N5: part_2.SCK, Компонент2.A4
  N6: part_2.SDA, Компонент2.A5
  N7: part_3.SW, Компонент2.D5_PWM
  N8: part_3.DT, Компонент2.D6_PWM
  N9: part_3.CLK, Компонент2.D7
  N10: Компонент2.D2, S1.Pin_3, S1.Pin_4, R1.Pin_1
  N11: Компонент2.D3_PWM, S2.Pin_3, S2.Pin_4, R2.Pin_1
  N12: Компонент2.D4, R3.Pin_1, S3.Pin_3, S3.Pin_4

custom parts:
  RFID-RC522-v2: A simple China made RFID-RC522 Reader; do check the pin labels, as this is a MFRC522 based clone.
  KY-040 Rotary encoder: KY-040 Rotary Encoder with switch on breakout borad from AZ Delivery
